# Fritzing sketch 202203110910 (saved by Fritzing 0.9.5d)
breadboards: 2

parts:
  M1 = DOIT Esp32 DevKit v1 (30 pins long, 11 pins width) [part_number=ESP32S-PIN30]
  DFRobot_DFPlayer_Mini1 = DFRobot DFPlayer Mini [part_number=DFR0299]
  SPKR1 = Loudspeaker
  Q1_NJL7502L = LTR-301 [package=ltr-301]
  R1 = Resistor [tolerance=±5% resistance=220k package=THT]

nets:
  N1: M1.D2, Q1_NJL7502L.C, R1.Pin_1
  N2: M1.D21, DFRobot_DFPlayer_Mini1.TX
  N3: M1.RX0, DFRobot_DFPlayer_Mini1.RX
  N4: M1.D22, DFRobot_DFPlayer_Mini1.GND-1, DFRobot_DFPlayer_Mini1.GND-2, Q1_NJL7502L.E
  N5: M1.D23, DFRobot_DFPlayer_Mini1.VCC
  N6: DFRobot_DFPlayer_Mini1.SPK_1, SPKR1.pin2
  N7: DFRobot_DFPlayer_Mini1.SPK_2, SPKR1.pin1

custom parts:
  DOIT Esp32 DevKit v1 (30 pins long, 11 pins width): The DOIT Esp32 DevKit v1 is one of the development board created by DOIT to evaluate the ESP-WROOM-32 module. It is based on the ESP32 microcontroller that boasts Wifi, Bluetooth, Ethernet and Low Power support all in a single chip. (vanepp) made breadboard work, adjusted pin numbering and labels and reduced size of schematic and cleaned up pcb. This chip is 30pins long (2 x15) and 11 pins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
